# Fritzing sketch HttpMega (saved by Fritzing 0.8.3b)
breadboards: 1

parts:
  LCD1 = LCD screen
  Part1 = Arduino Mega 2560 (Rev3)
  Part2 = Arduino Ethernet Shield (Rev3)
  LED1 = LED - 3mm [color="Green (560nm)" package="3 mm [THT]"]
  LED2 = LED - 3mm [color="Yellow (585nm)" package="3 mm [THT]"]
  LED3 = LED - 3mm [color="Red (633nm)" package="3 mm [THT]"]
  R1 = Resistor [tolerance=±5% resistance=1k package=THT]
  R2 = Resistor [tolerance=±5% resistance=680 package=THT]
  R3 = Resistor [tolerance=±5% resistance=1k package=THT]
  R4 = Resistor [tolerance=±5% resistance=1k package=THT]

nets:
  N1: LCD1.VSS, LCD1.R/W, R1.Pin_0, R2.Pin_0, R3.Pin_0, R4.Pin_1
  N2: LCD1.V0, R4.Pin_0
  N3: LCD1.RS, Part1.D8_PWM, Part2.D8
  N4: LCD1.E, Part1.D7_PWM, Part2.D7
  N5: LCD1.DB4, Part1.D6_PWM, Part2.PWM_D6
  N6: LCD1.DB5, Part1.D5_PWM, Part2.PWM_D5
  N7: LCD1.DB6, Part1.D3_PWM, Part2.PWM_D3
  N8: LCD1.DB7, Part1.D2_PWM, Part2.D2
  N9: Part1.A0, Part2.A0
  N10: Part1.A1, Part2.A1
  N11: Part1.A2, Part2.A2
  N12: Part1.A3, Part2.A3
  N13: Part1.A4, Part1.SDA, Part2.A4/SDA
  N14: Part1.A5, Part1.SCL, Part2.A5/SCL
  N15: Part1.AREF, Part2.AREF
  GND: Part1.GND, Part2.GND
  N16: Part1.D10_PWM, Part2.ETH_CS
  N17: Part1.D9_PWM, Part2.PWM_D9, LED1.anode
  N18: Part1.IOREF, Part2.IOREF
  N19: Part1.RESET, Part2.RESET
  3V3: Part1.3V3, Part2.3V3
  5V: Part1.5V, Part2.5V
  VIN: Part1.VIN, Part2.VIN
  N20: Part1.D0_RX0, Part2.RX/D0
  N21: Part1.D1_TX0, Part2.TX/D1
  N22: Part1.D4_PWM, Part2.SDCS
  N23: Part1.D22, LED3.anode
  N24: Part1.D23, LED2.anode
  N25: LED1.cathode, R1.Pin_1
  N26: LED2.cathode, R2.Pin_1
  N27: LED3.cathode, R3.Pin_1

notes:
  5V Power Supply
  9V - 12V Power Supply
  Do not connect pins 11,12 and 13
